// Logisim project lab4_encoder.circ as structural Verilog: 5 circuits, main circuit Encoder16x4
module Encoder16x4 (
  input  A0,
  input  A1,
  input  A2,
  input  A3,
  input  A4,
  input  A5,
  input  A6,
  input  A7,
  input  A8,
  input  A9,
  input  A10,
  input  A11,
  input  A12,
  input  A13,
  input  A14,
  input  A15
);

  wire or_1_out, or_2_out, or_3_out, or_4_out, xnor_1_out;
  wire [3:0] xor_4_out;

  or or_1 (or_1_out, A0, A1, A2, A3, A4, A5, A6, A7);
  ExactlyOne xor_1 (.out(xor_4_out[3]), .in0(or_1_out), .in1(xnor_1_out), .in2(xnor_1_out));
  or or_2 (or_2_out, A0, A1, A2, A3, A8, A9, A10, A11);
  ExactlyOne xor_2 (.out(xor_4_out[2]), .in0(or_2_out), .in1(xnor_1_out), .in2(xnor_1_out));
  // Probe on xor_4_out
  or or_3 (or_3_out, A0, A1, A4, A5, A8, A9, A12, A13);
  ExactlyOne xor_3 (.out(xor_4_out[1]), .in0(or_3_out), .in1(xnor_1_out), .in2(xnor_1_out));
  or or_4 (or_4_out, A0, A2, A4, A6, A8, A10, A12, A14);
  ExactlyOne xor_4 (.out(xor_4_out[0]), .in0(or_4_out), .in1(xnor_1_out), .in2(xnor_1_out));
  NotExactlyOne xnor_1 (
    .out(xnor_1_out), .in0(A0), .in1(A1), .in2(A2), .in3(A3), .in4(A4), .in5(A5), .in6(A6), .in7(A7),
    .in8(A8), .in9(A9), .in10(A10), .in11(A11), .in12(A12), .in13(A13), .in14(A14), .in15(A15));
  // Probe on xnor_1_out
endmodule

module Dencoder4X16 (
  input  [3:0] in_1
);

  wire a_out, b_out, c_out, D0_out, D1_out, D2_out, D3_out, D4_out, D5_out, D6_out, D7_out, D8_out, D9_out,
       d_out, DA_out, DB_out, DC_out, DD_out, DE_out, DF_out, e_out, f_out, g_out, not_1_out, not_2_out,
       not_3_out, not_4_out, not_5_out, not_6_out, not_7_out, not_8_out, not_9_out, not_10_out, not_11_out,
       not_12_out, not_13_out, not_14_out, not_15_out, not_16_out, not_17_out, not_18_out, not_19_out,
       not_20_out, not_21_out, not_22_out, not_23_out, not_24_out, not_25_out, not_26_out, not_27_out,
       not_28_out, not_29_out, not_30_out, not_31_out, not_32_out;

  not not_1 (not_1_out, in_1[3]);
  not not_2 (not_2_out, in_1[1]);
  not not_3 (not_3_out, in_1[2]);
  not not_4 (not_4_out, in_1[3]);
  not not_5 (not_5_out, in_1[0]);
  not not_6 (not_6_out, in_1[2]);
  not not_7 (not_7_out, in_1[3]);
  not not_8 (not_8_out, in_1[2]);
  not not_9 (not_9_out, in_1[3]);
  not not_10 (not_10_out, in_1[0]);
  not not_11 (not_11_out, in_1[1]);
  not not_12 (not_12_out, in_1[3]);
  not not_13 (not_13_out, in_1[1]);
  not not_14 (not_14_out, in_1[3]);
  not not_15 (not_15_out, in_1[0]);
  not not_16 (not_16_out, in_1[3]);
  not not_17 (not_17_out, in_1[3]);
  not not_18 (not_18_out, in_1[1]);
  not not_19 (not_19_out, in_1[1]);
  not not_20 (not_20_out, in_1[2]);
  not not_21 (not_21_out, in_1[0]);
  not not_22 (not_22_out, in_1[1]);
  not not_23 (not_23_out, in_1[2]);
  not not_24 (not_24_out, in_1[0]);
  not not_25 (not_25_out, in_1[2]);
  not not_26 (not_26_out, in_1[0]);
  not not_27 (not_27_out, in_1[2]);
  not not_28 (not_28_out, in_1[2]);
  not not_29 (not_29_out, in_1[0]);
  not not_30 (not_30_out, in_1[1]);
  not not_31 (not_31_out, in_1[1]);
  not not_32 (not_32_out, in_1[0]);
  and D0 (D0_out, not_21_out, not_22_out, not_23_out, not_1_out);
  and D1 (D1_out, in_1[0], not_2_out, not_3_out, not_4_out);
  and D2 (D2_out, not_5_out, in_1[1], not_6_out, not_7_out);
  and D3 (D3_out, in_1[0], in_1[1], not_8_out, not_9_out);
  and D4 (D4_out, not_10_out, not_11_out, in_1[2], not_12_out);
  and D5 (D5_out, in_1[0], not_13_out, in_1[2], not_14_out);
  and D6 (D6_out, not_15_out, in_1[1], in_1[2], not_16_out);
  and D7 (D7_out, in_1[0], in_1[1], in_1[2], not_17_out);
  and D8 (D8_out, not_24_out, not_18_out, not_25_out, in_1[3]);
  and D9 (D9_out, in_1[0], not_19_out, not_20_out, in_1[3]);
  and DA (DA_out, not_26_out, in_1[1], not_27_out, in_1[3]);
  and DB (DB_out, in_1[0], in_1[1], not_28_out, in_1[3]);
  and DC (DC_out, not_29_out, not_30_out, in_1[2], in_1[3]);
  and DD (DD_out, in_1[0], not_31_out, in_1[2], in_1[3]);
  and DE (DE_out, not_32_out, in_1[1], in_1[2], in_1[3]);
  and DF (DF_out, in_1[0], in_1[1], in_1[2], in_1[3]);
  or a (a_out, D0_out, D2_out, D3_out, D5_out, D6_out, D7_out, D8_out, D9_out, DA_out, DC_out, DE_out, DF_out);
  or b (b_out, D0_out, D1_out, D2_out, D3_out, D4_out, D7_out, D8_out, D9_out, DA_out, DD_out);
  or c (c_out, D0_out, D1_out, D3_out, D4_out, D5_out, D6_out, D7_out, D8_out, D9_out, DA_out, DB_out, DD_out);
  or d (d_out, D0_out, D2_out, D3_out, D5_out, D6_out, D8_out, D9_out, DB_out, DC_out, DD_out, DE_out);
  or e (e_out, D0_out, D2_out, D6_out, D8_out, DA_out, DB_out, DC_out, DD_out, DE_out, DF_out);
  or f (f_out, D0_out, D4_out, D5_out, D6_out, D8_out, D9_out, DA_out, DB_out, DC_out, DE_out, DF_out);
  or g (g_out, D2_out, D3_out, D4_out, D5_out, D6_out, D8_out, D9_out, DA_out, DB_out, DD_out, DE_out, DF_out);
  _7_Segment_Display u_7_segment_display_1 (
    .g(g_out), .f(f_out), .a(a_out), .b(b_out), .e(e_out), .d(d_out), .c(c_out));  // open: dp
endmodule

module Multiplexor (
  input  A0,
  input  A1,
  input  A2,
  input  A3,
  input  A4,
  input  A5,
  input  A6,
  input  A7,
  input  [2:0] Sel
);

  wire I0_out, I1_out, I2_out, I3_out, I4_out, I5_out, I6_out, I7_out, not_1_out, not_2_out, not_3_out,
       or_1_out;

  not not_1 (not_1_out, Sel[0]);
  not not_2 (not_2_out, Sel[1]);
  not not_3 (not_3_out, Sel[2]);
  and I0 (I0_out, A0, not_1_out, not_2_out, not_3_out);
  and I1 (I1_out, A1, Sel[0], not_2_out, not_3_out);
  and I2 (I2_out, A2, Sel[1], not_1_out, not_3_out);
  and I3 (I3_out, A3, Sel[0], Sel[1], not_3_out);
  and I4 (I4_out, A4, Sel[2], not_1_out, not_2_out);
  and I5 (I5_out, A5, Sel[0], not_2_out, Sel[2]);
  and I6 (I6_out, A6, not_1_out, Sel[1], Sel[2]);
  and I7 (I7_out, A7, Sel[0], Sel[1], Sel[2]);
  or or_1 (or_1_out, I0_out, I1_out, I2_out, I3_out, I4_out, I5_out, I6_out, I7_out);
  // Probe on or_1_out
endmodule

module Demultiplexor (
  input  DI,
  input  [2:0] Sel
);

  wire I0_out, I1_out, I2_out, I3_out, I4_out, I5_out, I6_out, I7_out, not_1_out, not_2_out, not_3_out;

  not not_1 (not_1_out, Sel[0]);
  not not_2 (not_2_out, Sel[1]);
  not not_3 (not_3_out, Sel[2]);
  // Probe on I0_out
  and I0 (I0_out, DI, not_1_out, not_2_out, not_3_out);
  // Probe on I1_out
  and I1 (I1_out, DI, Sel[0], not_2_out, not_3_out);
  // Probe on I2_out
  and I2 (I2_out, DI, Sel[1], not_1_out, not_3_out);
  // Probe on I3_out
  and I3 (I3_out, DI, Sel[0], Sel[1], not_3_out);
  // Probe on I4_out
  and I4 (I4_out, DI, Sel[2], not_1_out, not_2_out);
  // Probe on I5_out
  and I5 (I5_out, DI, Sel[0], not_2_out, Sel[2]);
  // Probe on I6_out
  and I6 (I6_out, DI, not_1_out, Sel[1], Sel[2]);
  // Probe on I7_out
  and I7 (I7_out, DI, Sel[0], Sel[1], Sel[2]);
endmodule

module ALU (
  input  in_1,
  input  [7:0] A,
  input  in_3,
  input  [7:0] B,
  input  [2:0] Sel
);

  wire [7:0] multiplexer_1_out, R0, R1, R2, R3, R4, R5, R6, R7;

  Adder8 adder8_1 (.CIN(in_1), .A(A), .B(B), .out_4(R0));  // open: out_5
  Subtractor8 subtractor8_1 (.CIN(in_3), .A(A), .B(B), .out_4(R1));  // open: out_5
  assign R2 = A & B;  // AND_Gate and_1, 8 bits wide
  assign R3 = A | B;  // OR_Gate or_1, 8 bits wide
  assign R4 = A ^ B;  // XOR_Gate xor_1, 8 bits wide
  Shifter shifter_1 (.in(A), .\dist (3'b111), .out(R5));
  Shifter #(.shift("lr")) shifter_2 (.in(A), .\dist (3'b111), .out(R6));
  Shifter shifter_3 (.in(A), .\dist (3'b111), .out(R7));
  // Probe on multiplexer_1_out
  Multiplexer #(.select(3), .width(8)) multiplexer_1 (
    .in0(R0), .in1(R1), .in2(R2), .in3(R3), .in4(R4), .in5(R5), .in6(R6), .in7(R7), .out(multiplexer_1_out),
    .sel(Sel));
endmodule
