// Logisim project lab3.circ as structural Verilog: 4 circuits, main circuit FullAdder
module FullAdder (
  input  A,
  input  B,
  input  CIN,
  output S,
  output Cout
);

  wire and_1_out, and_2_out, xor_1_out;

  xor xor_1 (xor_1_out, A, B);
  xor xor_2 (S, xor_1_out, CIN);
  and and_1 (and_1_out, xor_1_out, CIN);
  and and_2 (and_2_out, B, A);
  xor xor_3 (Cout, and_1_out, and_2_out);
endmodule

module Adder8 (
  input  CIN,
  input  [7:0] A,
  input  [7:0] B,
  output [7:0] out_4,
  output out_5
);

  wire fulladder_1_cout, fulladder_2_cout, fulladder_3_cout, fulladder_4_cout, fulladder_5_cout,
       fulladder_6_cout, fulladder_7_cout;

  FullAdder fulladder_1 (.A(A[0]), .B(B[0]), .CIN(CIN), .S(out_4[0]), .Cout(fulladder_1_cout));
  FullAdder fulladder_2 (.A(A[1]), .B(B[1]), .CIN(fulladder_1_cout), .S(out_4[1]), .Cout(fulladder_2_cout));
  FullAdder fulladder_3 (.A(A[2]), .B(B[2]), .CIN(fulladder_2_cout), .S(out_4[2]), .Cout(fulladder_3_cout));
  FullAdder fulladder_4 (.A(A[3]), .B(B[3]), .CIN(fulladder_3_cout), .S(out_4[3]), .Cout(fulladder_4_cout));
  FullAdder fulladder_5 (.A(A[4]), .B(B[4]), .CIN(fulladder_4_cout), .S(out_4[4]), .Cout(fulladder_5_cout));
  FullAdder fulladder_6 (.A(A[5]), .B(B[5]), .CIN(fulladder_5_cout), .S(out_4[5]), .Cout(fulladder_6_cout));
  FullAdder fulladder_7 (.A(A[6]), .B(B[6]), .CIN(fulladder_6_cout), .S(out_4[6]), .Cout(fulladder_7_cout));
  FullAdder fulladder_8 (.A(A[7]), .B(B[7]), .CIN(fulladder_7_cout), .S(out_4[7]), .Cout(out_5));
endmodule

module Subtractor8 (
  input  CIN,
  input  [7:0] A,
  input  [7:0] B,
  output [7:0] out_4,
  output out_5
);

  wire fulladder_1_cout, fulladder_2_cout, fulladder_3_cout, fulladder_4_cout, fulladder_5_cout,
       fulladder_6_cout, fulladder_7_cout;
  wire [7:0] not_1_out;

  assign not_1_out = ~B;  // NOT_Gate not_1, 8 bits wide
  FullAdder fulladder_1 (.A(A[0]), .B(not_1_out[0]), .CIN(CIN), .S(out_4[0]), .Cout(fulladder_1_cout));
  FullAdder fulladder_2 (.A(A[1]), .B(not_1_out[1]), .CIN(fulladder_1_cout), .S(out_4[1]), .Cout(fulladder_2_cout));
  FullAdder fulladder_3 (.A(A[2]), .B(not_1_out[2]), .CIN(fulladder_2_cout), .S(out_4[2]), .Cout(fulladder_3_cout));
  FullAdder fulladder_4 (.A(A[3]), .B(not_1_out[3]), .CIN(fulladder_3_cout), .S(out_4[3]), .Cout(fulladder_4_cout));
  FullAdder fulladder_5 (.A(A[4]), .B(not_1_out[4]), .CIN(fulladder_4_cout), .S(out_4[4]), .Cout(fulladder_5_cout));
  FullAdder fulladder_6 (.A(A[5]), .B(not_1_out[5]), .CIN(fulladder_5_cout), .S(out_4[5]), .Cout(fulladder_6_cout));
  FullAdder fulladder_7 (.A(A[6]), .B(not_1_out[6]), .CIN(fulladder_6_cout), .S(out_4[6]), .Cout(fulladder_7_cout));
  FullAdder fulladder_8 (.A(A[7]), .B(not_1_out[7]), .CIN(fulladder_7_cout), .S(out_4[7]), .Cout(out_5));
endmodule

module Umn4x4 (
  input  [3:0] B,
  input  [3:0] A,
  output p1,
  output p2,
  output p3,
  output p4,
  output p5,
  output p6,
  output p7,
  output p8
);

  wire adder_1_cout, adder_2_cout, adder_2_out, adder_3_cout, adder_3_out, adder_4_cout, adder_4_out,
       adder_5_cout, adder_6_cout, adder_6_out, adder_7_cout, adder_7_out, adder_8_cout, adder_8_out,
       adder_9_cout, adder_10_cout, adder_11_cout, M1_2_out, M1_3_out, M1_4_out, M2_1_out, M2_2_out,
       M2_3_out, M2_4_out, M3_1_out, M3_2_out, M3_3_out, M3_4_out, M4_1_out, M4_2_out, M4_3_out, M4_4_out;

  and M1_1 (p1, B[0], A[0]);
  and M1_2 (M1_2_out, B[0], A[1]);
  and M1_3 (M1_3_out, B[0], A[2]);
  and M1_4 (M1_4_out, B[0], A[3]);
  and M2_1 (M2_1_out, B[1], A[0]);
  and M2_2 (M2_2_out, B[1], A[1]);
  and M2_3 (M2_3_out, B[1], A[2]);
  and M2_4 (M2_4_out, B[1], A[3]);
  Adder #(.width(1)) adder_1 (.a(M1_2_out), .b(M2_1_out), .out(p2), .cin(1'b0), .cout(adder_1_cout));
  Adder #(.width(1)) adder_2 (.a(M1_3_out), .b(M2_2_out), .out(adder_2_out), .cin(adder_1_cout), .cout(adder_2_cout));
  Adder #(.width(1)) adder_3 (.a(M1_4_out), .b(M2_3_out), .out(adder_3_out), .cin(adder_2_cout), .cout(adder_3_cout));
  Adder #(.width(1)) adder_4 (.a(1'b0), .b(M2_4_out), .out(adder_4_out), .cin(adder_3_cout), .cout(adder_4_cout));
  and M3_1 (M3_1_out, B[2], A[0]);
  and M3_2 (M3_2_out, B[2], A[1]);
  and M3_3 (M3_3_out, B[2], A[2]);
  and M3_4 (M3_4_out, B[2], A[3]);
  Adder #(.width(1)) adder_5 (.a(M3_1_out), .b(adder_2_out), .out(p3), .cin(1'b0), .cout(adder_5_cout));
  Adder #(.width(1)) adder_6 (
    .a(M3_2_out), .b(adder_3_out), .out(adder_6_out), .cin(adder_5_cout), .cout(adder_6_cout));
  Adder #(.width(1)) adder_7 (
    .a(M3_3_out), .b(adder_4_out), .out(adder_7_out), .cin(adder_6_cout), .cout(adder_7_cout));
  Adder #(.width(1)) adder_8 (
    .a(M3_4_out), .b(adder_4_cout), .out(adder_8_out), .cin(adder_7_cout), .cout(adder_8_cout));
  and M4_1 (M4_1_out, B[3], A[0]);
  and M4_2 (M4_2_out, B[3], A[1]);
  and M4_3 (M4_3_out, B[3], A[2]);
  and M4_4 (M4_4_out, B[3], A[3]);
  Adder #(.width(1)) adder_9 (.a(M4_1_out), .b(adder_6_out), .out(p4), .cin(1'b0), .cout(adder_9_cout));
  Adder #(.width(1)) adder_10 (.a(M4_2_out), .b(adder_7_out), .out(p5), .cin(adder_9_cout), .cout(adder_10_cout));
  Adder #(.width(1)) adder_11 (.a(M4_3_out), .b(adder_8_out), .out(p6), .cin(adder_10_cout), .cout(adder_11_cout));
  Adder #(.width(1)) adder_12 (.a(M4_4_out), .b(adder_8_cout), .out(p7), .cin(adder_11_cout), .cout(p8));
endmodule
