// Logisim project lab05.circ as structural Verilog
module async_RS_trigger (
  input  R,
  input  S,
  output Q,
  output Qn
);

  nor nor_1 (Q, R, Qn);
  nor nor_2 (Qn, S, Q);
endmodule

module sync_RS_trigger (
  input  R,
  input  S,
  input  C,
  output Q,
  output Qn
);

  wire and_1_out, and_2_out;

  and and_1 (and_1_out, R, C);
  and and_2 (and_2_out, S, C);
  async_RS_trigger async_rs_trigger_1 (.R(and_1_out), .S(and_2_out), .Q(Q), .Qn(Qn));
endmodule

module sync_D_trigger_level (
  input  D,
  input  E,
  output Q,
  output Qn
);

  wire not_1_out;

  not not_1 (not_1_out, D);
  sync_RS_trigger sync_rs_trigger_1 (.R(not_1_out), .S(D), .C(E), .Q(Q), .Qn(Qn));
endmodule

module sync_D_trigger_front (
  input  D,
  input  CLK,
  output Q,
  output Qn
);

  wire not_1_out, sync_d_trigger_level_1_q;

  not not_1 (not_1_out, CLK);
  sync_D_trigger_level sync_d_trigger_level_1 (.D(D), .E(not_1_out), .Q(sync_d_trigger_level_1_q));  // open: Qn
  sync_D_trigger_level sync_d_trigger_level_2 (.D(sync_d_trigger_level_1_q), .E(CLK), .Q(Q), .Qn(Qn));
endmodule

module sync_register_8bit (
  input  [7:0] D,
  input  E,
  output [7:0] out_3
);

  sync_D_trigger_front sync_d_trigger_front_1 (.D(D[0]), .CLK(E), .Q(out_3[0]));  // open: Qn
  sync_D_trigger_front sync_d_trigger_front_2 (.D(D[1]), .CLK(E), .Q(out_3[1]));  // open: Qn
  sync_D_trigger_front sync_d_trigger_front_3 (.D(D[2]), .CLK(E), .Q(out_3[2]));  // open: Qn
  sync_D_trigger_front sync_d_trigger_front_4 (.D(D[3]), .CLK(E), .Q(out_3[3]));  // open: Qn
  sync_D_trigger_front sync_d_trigger_front_5 (.D(D[4]), .CLK(E), .Q(out_3[4]));  // open: Qn
  sync_D_trigger_front sync_d_trigger_front_6 (.D(D[5]), .CLK(E), .Q(out_3[5]));  // open: Qn
  sync_D_trigger_front sync_d_trigger_front_7 (.D(D[6]), .CLK(E), .Q(out_3[6]));  // open: Qn
  sync_D_trigger_front sync_d_trigger_front_8 (.D(D[7]), .CLK(E), .Q(out_3[7]));  // open: Qn
endmodule

module incrementer_4bit (
  input  [3:0] X,
  output [3:0] Y
);

  wire and_1_out, and_2_out;

  not not_1 (Y[0], X[0]);
  xor xor_1 (Y[1], X[0], X[1]);
  and and_1 (and_1_out, X[0], X[1]);
  and and_2 (and_2_out, X[0], X[1], X[2]);
  xor xor_2 (Y[2], and_1_out, X[2]);
  xor xor_3 (Y[3], and_2_out, X[3]);
endmodule

module L_8_bit_memory_summator (
  input  [7:0] A,
  input  [7:0] B,
  input  FromLatch,
  input  Save,
  output [7:0] S,
  output CO
);

  wire [7:0] multiplexer_1_out, sync_register_8bit_1_out_3;

  Multiplexer #(.width(8)) multiplexer_1 (
    .in0(B), .in1(sync_register_8bit_1_out_3), .out(multiplexer_1_out), .sel(FromLatch));
  sync_register_8bit sync_register_8bit_1 (.D(S), .E(Save), .out_3(sync_register_8bit_1_out_3));
  // Adder8 adder8_1: pin names not known; wires that end beside it: 1'b0, A, multiplexer_1_out, S, CO
endmodule

module L_8_bit_accum_summator (
  input  [7:0] A,
  input  Clr,
  input  Add,
  output [7:0] out_4
);

  wire [7:0] adder8_1_p4;

  Register register_1 (.D(adder8_1_p4), .clk(Add), .Q(out_4), .clr(Clr));  // open: en
  // Adder8 adder8_1: pin names not known; wires that end beside it: 1'b0, A, out_4, adder8_1_p4
endmodule

module L_8_bit_8_cell_memory (
  input  [7:0] DataIn,
  input  [2:0] WriteAddr,
  input  [2:0] ReadAddr,
  input  CLK,
  input  WE,
  output [7:0] Dataout
);

  wire demultiplexer_1_out0, demultiplexer_1_out1, demultiplexer_1_out2, demultiplexer_1_out3,
       demultiplexer_1_out4, demultiplexer_1_out5, demultiplexer_1_out6, demultiplexer_1_out7;
  wire [7:0] register_1_q, register_2_q, register_3_q, register_4_q, register_5_q, register_6_q,
       register_7_q, register_8_q;

  Register register_1 (.D(DataIn), .en(demultiplexer_1_out0), .clk(CLK), .Q(register_1_q));  // open: clr
  Register register_2 (.D(DataIn), .en(demultiplexer_1_out1), .clk(CLK), .Q(register_2_q));  // open: clr
  Register register_3 (.D(DataIn), .en(demultiplexer_1_out2), .clk(CLK), .Q(register_3_q));  // open: clr
  Register register_4 (.D(DataIn), .en(demultiplexer_1_out3), .clk(CLK), .Q(register_4_q));  // open: clr
  Register register_5 (.D(DataIn), .en(demultiplexer_1_out4), .clk(CLK), .Q(register_5_q));  // open: clr
  Register register_6 (.D(DataIn), .en(demultiplexer_1_out5), .clk(CLK), .Q(register_6_q), .clr(demultiplexer_1_out6));
  Register register_7 (.D(DataIn), .en(demultiplexer_1_out6), .clk(CLK), .Q(register_7_q));  // open: clr
  Register register_8 (.D(DataIn), .en(demultiplexer_1_out7), .clk(CLK), .Q(register_8_q));  // open: clr
  Demultiplexer #(.select(3)) demultiplexer_1 (
    .out0(demultiplexer_1_out0), .out1(demultiplexer_1_out1), .out2(demultiplexer_1_out2),
    .out3(demultiplexer_1_out3), .out4(demultiplexer_1_out4), .out5(demultiplexer_1_out5),
    .out6(demultiplexer_1_out6), .out7(demultiplexer_1_out7), .in(WE), .sel(WriteAddr));
  Multiplexer #(.select(3), .width(8)) multiplexer_1 (
    .in0(register_1_q), .in1(register_2_q), .in2(register_3_q), .in3(register_4_q), .in4(register_5_q),
    .in5(register_6_q), .in6(register_7_q), .in7(register_8_q), .out(Dataout), .sel(ReadAddr));
endmodule
