// Logisim project lab1_var9.circ as structural Verilog: 1 circuit, main circuit lab01
module lab01 (
  input  x3,
  input  x2,
  input  x1,
  input  x0,
  output Y2,
  output Y1,
  output Y0
);

  wire and_1_out, and_2_out, and_3_out, and_4_out, not_1_out, not_2_out, not_3_out, not_4_out, not_5_out;

  not not_1 (not_1_out, x3);
  and and_1 (and_1_out, not_1_out, x1);
  not not_2 (not_2_out, x3);
  and and_2 (and_2_out, not_2_out, x2);
  not not_3 (not_3_out, x3);
  not not_4 (not_4_out, x1);
  and and_3 (and_3_out, not_3_out, not_4_out, x0);
  not not_5 (not_5_out, x3);
  and and_4 (and_4_out, not_5_out, x2);
  or or_1 (Y1, and_1_out, and_2_out);
  or or_2 (Y0, and_3_out, and_4_out);

  assign Y2 = x3;
endmodule
