// Logisim project lab3.circ as structural Verilog: 3 circuits, main circuit FullAdder
module FullAdder (
  input  A,
  input  B,
  input  CIN,
  output S,
  output Cout
);

  wire and_1_out, and_2_out, xor_1_out;

  xor xor_1 (xor_1_out, A, B);
  xor xor_2 (S, xor_1_out, CIN);
  and and_1 (and_1_out, xor_1_out, CIN);
  and and_2 (and_2_out, B, A);
  xor xor_3 (Cout, and_1_out, and_2_out);
endmodule

module Adder8 (
  input  CIN,
  input  [7:0] A,
  input  [7:0] B,
  output [7:0] out_4,
  output out_5
);

  wire fulladder_1_cout, fulladder_2_cout, fulladder_3_cout, fulladder_4_cout, fulladder_5_cout,
       fulladder_6_cout, fulladder_7_cout;

  FullAdder fulladder_1 (.A(A[0]), .B(B[0]), .CIN(CIN), .S(out_4[0]), .Cout(fulladder_1_cout));
  FullAdder fulladder_2 (.A(A[1]), .B(B[1]), .CIN(fulladder_1_cout), .S(out_4[1]), .Cout(fulladder_2_cout));
  FullAdder fulladder_3 (.A(A[2]), .B(B[2]), .CIN(fulladder_2_cout), .S(out_4[2]), .Cout(fulladder_3_cout));
  FullAdder fulladder_4 (.A(A[3]), .B(B[3]), .CIN(fulladder_3_cout), .S(out_4[3]), .Cout(fulladder_4_cout));
  FullAdder fulladder_5 (.A(A[4]), .B(B[4]), .CIN(fulladder_4_cout), .S(out_4[4]), .Cout(fulladder_5_cout));
  FullAdder fulladder_6 (.A(A[5]), .B(B[5]), .CIN(fulladder_5_cout), .S(out_4[5]), .Cout(fulladder_6_cout));
  FullAdder fulladder_7 (.A(A[6]), .B(B[6]), .CIN(fulladder_6_cout), .S(out_4[6]), .Cout(fulladder_7_cout));
  FullAdder fulladder_8 (.A(A[7]), .B(B[7]), .CIN(fulladder_7_cout), .S(out_4[7]), .Cout(out_5));
endmodule

module Subtractor8 (
  input  CIN,
  input  [7:0] A,
  input  [7:0] B,
  output [7:0] out_4,
  output out_5
);

  wire fulladder_1_cout, fulladder_2_cout, fulladder_3_cout, fulladder_4_cout, fulladder_5_cout,
       fulladder_6_cout, fulladder_7_cout;
  wire [7:0] not_1_out;

  assign not_1_out = ~B;  // NOT_Gate not_1, 8 bits wide
  FullAdder fulladder_1 (.A(A[0]), .B(not_1_out[0]), .CIN(CIN), .S(out_4[0]), .Cout(fulladder_1_cout));
  FullAdder fulladder_2 (.A(A[1]), .B(not_1_out[1]), .CIN(fulladder_1_cout), .S(out_4[1]), .Cout(fulladder_2_cout));
  FullAdder fulladder_3 (.A(A[2]), .B(not_1_out[2]), .CIN(fulladder_2_cout), .S(out_4[2]), .Cout(fulladder_3_cout));
  FullAdder fulladder_4 (.A(A[3]), .B(not_1_out[3]), .CIN(fulladder_3_cout), .S(out_4[3]), .Cout(fulladder_4_cout));
  FullAdder fulladder_5 (.A(A[4]), .B(not_1_out[4]), .CIN(fulladder_4_cout), .S(out_4[4]), .Cout(fulladder_5_cout));
  FullAdder fulladder_6 (.A(A[5]), .B(not_1_out[5]), .CIN(fulladder_5_cout), .S(out_4[5]), .Cout(fulladder_6_cout));
  FullAdder fulladder_7 (.A(A[6]), .B(not_1_out[6]), .CIN(fulladder_6_cout), .S(out_4[6]), .Cout(fulladder_7_cout));
  FullAdder fulladder_8 (.A(A[7]), .B(not_1_out[7]), .CIN(fulladder_7_cout), .S(out_4[7]), .Cout(out_5));
endmodule
